# Fritzing sketch Automated_Hand_sanitizer_despenser (saved by Fritzing 0.8.7b)

parts:
  PIR1 = PIR sensor
  Part1 = Arduino Uno (Rev3)
  J1 = Basic Servo

nets:
  VDD: PIR1.VDD, Part1.5V, J1.vcc
  N1: PIR1.SIG, Part1.D12/MISO
  GND: PIR1.GND, Part1.GND, J1.gnd
  N2: Part1.D11_PWM/MOSI, J1.pulse
